# Fritzing sketch circuitFritzing (saved by Fritzing 0.9.3b)
breadboards: 2

parts:
  Slave_Arduino = Arduino Nano (Rev3.0)
  R1 = Resistor [tolerance=±5% resistance=220 package="2512 [SMD]"]
  LED1 = LED - 3mm [color="Red (633nm)" package="3 mm [THT]"]
  Hc-05_Slave = Bluetooth HC-05 Macho
  Master_Aruino = Arduino Mega 2560 (Rev3)
  Hc-05_Master = Bluetooth HC-05 Macho
  B1k_Potentiometer = POT [package=pot_alpha_rv16af-20]

nets:
  N1: Slave_Arduino.D1/TX, Hc-05_Slave.RXD
  N2: Slave_Arduino.D0/RX, Hc-05_Slave.TXD
  GND: Slave_Arduino.GND, R1.Pin_1, LED1.cathode, LED1.anode, Hc-05_Slave.GND
  N3: Slave_Arduino.D9, R1.Pin_0
  5V: Slave_Arduino.5V, Hc-05_Slave.VCC
  N4: Master_Aruino.A0, B1k_Potentiometer.S
  GND_2: Master_Aruino.GND, Hc-05_Master.GND, B1k_Potentiometer.A, B1k_Potentiometer.E
  5V_2: Master_Aruino.5V, Hc-05_Master.VCC
  N5: Master_Aruino.D0_RX0, Hc-05_Master.TXD
  N6: Master_Aruino.D1_TX0, Hc-05_Master.RXD

// code stored in the sketch: slave.ino
void setup() {
  Serial.begin(9600);
  pinMode(9, OUTPUT); // Set pin 9 as an output
}

void loop() {
    digitalWrite(9, HIGH);
  }
}
